# Fritzing sketch fritzing (saved by Fritzing 0.8.7b)
breadboards: 1

parts:
  U1 = NodeMCU V3.0
  BC547 = NPN-Transistor [package="TO92 [THT]"]
  R1 = Resistor [tolerance=±5% resistance=220 package=THT]
  5V_1A_DC = Power plug
  LED1 = LEDs [package=led10mm]
  230V_AC_Power_supply = Power plug

nets:
  N1: U1.D0, R1.Pin_1
  GND: U1.GND, 5V_1A_DC.GND
  VIN: U1.Vin, BC547.C, 5V_1A_DC.VCC
  N2: BC547.B, R1.Pin_0
  N3: LED1.A, 230V_AC_Power_supply.VCC

custom parts:
  NodeMCU V3.0: ESP8266 based NodeMCU
  LEDs: LEDs Standard schematic elements and footprints for 5mm, 3mm, 1206, and 0603 sized LEDs. 5mm - Spark Fun Electronics SKU : COM-00529 (and others)
